# Fritzing sketch PullupResistorDiagram (saved by Fritzing 0.9.10b)
breadboards: 1

parts:
  Part1 = Arduino Uno (Rev3)
  R1 = Resistor [tolerance=±5% resistance=2000 package="0805 [SMD]"]
  J4 = female pin header, 3 pins [form="♀ (female)"]
  J5 = Basic Servo
  J6 = female pin header, 2 pins [form="♀ (female)"]

nets:
  N1: Part1.D2, R1.Pin_1, J4.pin1, J5.pulse
  N2: Part1.5V, R1.Pin_0
  GND: Part1.GND, J4.pin3, J5.gnd, J6.pin1
  N3: J4.pin2, J5.vcc, J6.pin2

notes:
  To servo power supply
  USB to computer
